// Digital circuit 2-bit_UD_counter.dig as structural Verilog
module _2_bit_UD_counter (
  input  Increment_Decrement__1_0,
  input  Clock,
  output _0_bit_position,
  output _1_bit_position
);

  wire and_1_out, and_2_out, not_1_out, not_2_out, not_3_out, or_1_out;

  not not_1 (not_1_out, _0_bit_position);
  not not_2 (not_2_out, Increment_Decrement__1_0);
  and and_1 (and_1_out, not_1_out, not_2_out);
  and and_2 (and_2_out, _0_bit_position, Increment_Decrement__1_0);
  or or_1 (or_1_out, and_1_out, and_2_out);
  not not_3 (not_3_out, _0_bit_position);
  JK_FF Q_1 (.J(or_1_out), .C(Clock), .K(or_1_out), .Q(_1_bit_position));  // open: nQ
  JK_FF Q_0 (.J(not_3_out), .C(Clock), .K(_0_bit_position), .Q(_0_bit_position));  // open: nQ
  LED led_1 (.in(_1_bit_position));
  LED led_2 (.in(_0_bit_position));
endmodule
