// Digital circuit 3-bit_Pattern_110.dig as structural Verilog
module _3_bit_Pattern_110 (
  input  \input ,
  input  Clock,
  output Detection,
  output _0_Alert,
  output _0__Alert
);

  wire and_1_out, and_2_out, and_3_out, and_4_out, and_5_out, and_6_out, and_7_out, not_1_out, not_2_out,
       not_3_out, or_1_out, or_2_out, or_3_out, S_0_nq, S_1_nq;

  not not_1 (not_1_out, \input );
  and and_1 (and_1_out, _0_Alert, \input );
  and and_2 (and_2_out, _0_Alert, _0__Alert);
  not not_2 (not_2_out, \input );
  and and_3 (and_3_out, S_1_nq, _0__Alert, \input );
  and and_4 (and_4_out, _0_Alert, _0__Alert, not_1_out);
  and and_5 (and_5_out, _0_Alert, S_0_nq, not_2_out);
  and and_6 (and_6_out, S_1_nq, S_0_nq, \input );
  and and_7 (and_7_out, S_1_nq, _0__Alert, \input );
  or or_1 (or_1_out, and_1_out, and_2_out);
  or or_2 (or_2_out, and_5_out, and_6_out);
  or or_3 (or_3_out, and_3_out, and_4_out);
  RS_FF S_1 (.S(and_7_out), .C(Clock), .R(or_1_out), .Q(_0_Alert), .nQ(S_1_nq));
  RS_FF S_0 (.S(or_2_out), .C(Clock), .R(or_3_out), .Q(_0__Alert), .nQ(S_0_nq));
  not not_3 (not_3_out, \input );
  and and_8 (Detection, _0_Alert, S_0_nq, not_3_out);
  LED led_1 (.in(Detection));
endmodule
