// Digital circuit 4-Bit Register_to_ALU.dig as structural Verilog
module _4_Bit_Register_to_ALU (
  input  Clock,
  input  [2:0] Op_Select,
  input  [1:0] Read_Select__1,
  input  [1:0] Read_Select__2,
  input  [1:0] Select_Write,
  input  [3:0] Write_Data,
  input  [7:0] Ctrl_Register,
  output [3:0] Output
);

  wire [3:0] register_file_4_bit_1_p7, register_file_4_bit_1_p8;

  // Register_file_4_bit register_file_4_bit_1: pin names not known; wires that end beside it: Read_Select__1, Read_Select__2, Clock, Write_Data, Select_Write, Ctrl_Register, register_file_4_bit_1_p7, register_file_4_bit_1_p8
  _4_bit_ALU _4_bit_alu_1 (
    .A(register_file_4_bit_1_p7), .B(register_file_4_bit_1_p8), .S1_S0_C_in(Op_Select), .Output(Output));  // open: Overflow
endmodule
