// Digital circuit 4-bit processor.dig as structural Verilog
module _4_bit_processor (
  input  [1:0] IR_Ctrl,
  input  [1:0] Memory_Ctrl,
  input  [3:0] Memory_Input,
  input  [1:0] PC_Ctrl,
  input  Sim_Clk,
  output [1:0] PC_Output,
  output [15:0] Instruction_Out,
  output [3:0] Read_Out_1,
  output [3:0] Read_Out_2,
  output [3:0] ALU_Out
);

  wire ir_memory_module_1_p8;
  wire [7:0] multiplexer_1_out, registerfile_write_ctrl_1_p2;

  // IR_Memory_Module ir_memory_module_1: pin names not known; wires that end beside it: PC_Ctrl, Sim_Clk, Memory_Input, Memory_Ctrl, IR_Ctrl, PC_Output, Instruction_Out, ir_memory_module_1_p8
  // RegisterFIle_Write_ctrl registerfile_write_ctrl_1: pin names not known; wires that end beside it: Instruction_Out[1:0], registerfile_write_ctrl_1_p2
  Multiplexer #(.Bits(8)) multiplexer_1 (
    .sel(ir_memory_module_1_p8), .in_0({8{1'b0}}), .in_1(registerfile_write_ctrl_1_p2),
    .out(multiplexer_1_out));
  // Register_file_4_bit register_file_4_bit_1: pin names not known; wires that end beside it: Instruction_Out[5:4], Instruction_Out[3:2], Sim_Clk, ALU_Out, Instruction_Out[1:0], multiplexer_1_out, Read_Out_1, Read_Out_2
  _4_bit_ALU _4_bit_alu_1 (
    .A(Read_Out_1), .B(Read_Out_2), .S1_S0_C_in(Instruction_Out[8:6]), .Output(ALU_Out));  // open: Overflow

  // Notes on the sheet:
  //   PC_Ctrl: default 1
endmodule

/* Test case Circuit Testing:
Sim-Clk IR-Ctrl Memory-Ctrl Memory-Input PC-Ctrl PC-Output Instruction-Out Read-Out-1 Read-Out-2 ALU-Out
c 0 1 0x0 1 x x x x x 
c 0 1 0x4 1 x x x x x 
c 0 1 0x1 1 x x x x x 
c 0 1 0x0 1 x x x x x 

c 0 1 0x0 1 x x x x x 
c 0 1 0x4 1 x x x x x 
c 0 1 0x1 1 x x x x x 
c 0 1 0x0 1 x x x x x 

c 0 1 0x5 1 x x x x x 
c 0 1 0x5 1 x x x x x 
c 0 1 0x1 1 x x x x x 
c 0 1 0x0 1 x x x x x 

c 0 1 0x6 1 x x x x x 
c 0 1 0x0 1 x x x x x 
c 0 1 0x0 1 x x x x x 
c 0 1 0x0 1 x x x x x 

c 1 0 0x0 1 x x x x x  
c 1 0 0x4 1 x x x x x 
c 1 0 0x1 1 x x x x x 
c 1 0 0x0 1 x x x x x 

c 1 0 0x0 1 x x x x x 
c 1 0 0x4 1 x x x x x 
c 1 0 0x1 1 x x x x x 
c 1 0 0x0 1 x x x x x 

c 1 0 0x5 1 x x x x x 
c 1 0 0x5 1 x x x x x 
c 1 0 0x1 1 x x x x x 
c 1 0 0x0 1 x x x x x 

c 1 0 0x6 1 x x x x x 
c 1 0 0x0 1 x x x x x 
c 1 0 0x0 1 x x x x x 
c 1 0 0x0 1 x x x x x 
*/
