// Digital circuit Assignment_one_2-Bit Multiplier.dig as structural Verilog
module Assignment_one_2_Bit_Multiplier (
  input  A_1,
  input  A_0,
  input  B_1,
  input  B_0,
  output P_3,
  output P_2,
  output P_1,
  output P_0
);

  wire and_2_out, and_3_out, and_4_out, and_5_out, and_6_out, and_7_out, not_1_out, not_2_out, not_3_out,
       not_4_out, not_5_out, not_6_out;

  not not_1 (not_1_out, B_1);
  not not_2 (not_2_out, A_0);
  not not_3 (not_3_out, A_1);
  not not_4 (not_4_out, B_0);
  not not_5 (not_5_out, A_0);
  not not_6 (not_6_out, B_0);
  and and_1 (P_0, A_0, B_0);
  and and_2 (and_2_out, A_1, not_1_out, B_0);
  and and_3 (and_3_out, A_1, not_2_out, B_0);
  and and_4 (and_4_out, not_3_out, A_0, B_1);
  and and_5 (and_5_out, A_0, B_1, not_4_out);
  and and_6 (and_6_out, A_1, not_5_out, B_1);
  and and_7 (and_7_out, A_1, B_1, not_6_out);
  and and_8 (P_3, A_1, A_0, B_1, B_0);
  or or_1 (P_1, and_2_out, and_3_out, and_4_out, and_5_out);
  or or_2 (P_2, and_6_out, and_7_out);
  LED led_1 (.in(P_0));
  LED led_2 (.in(P_1));
  LED led_3 (.in(P_2));
  LED led_4 (.in(P_3));
endmodule
