// Digital circuit Assignmnet_One_Solo_4-Chained-Full-Adder.dig as structural Verilog
module Assignmnet_One_Solo_4_Chained_Full_Adder (
  input  [3:0] B,
  input  [3:0] A,
  input  C_in,
  output [3:0] Sum,
  output Overflow_Alert
);

  wire B_0_c_out, B_1_c_out, B_2_c_out;

  Assignment_One_Solo_Full_Adder B_3 (.A(A[3]), .B(B[3]), .C_in(B_2_c_out), .Sum(Sum[3]), .C_out(Overflow_Alert));
  Assignment_One_Solo_Full_Adder B_2 (.A(A[2]), .B(B[2]), .C_in(B_1_c_out), .Sum(Sum[2]), .C_out(B_2_c_out));
  Assignment_One_Solo_Full_Adder B_1 (.A(A[1]), .B(B[1]), .C_in(B_0_c_out), .Sum(Sum[1]), .C_out(B_1_c_out));
  Assignment_One_Solo_Full_Adder B_0 (.A(A[0]), .B(B[0]), .C_in(C_in), .Sum(Sum[0]), .C_out(B_0_c_out));
  LED led_1 (.in(Overflow_Alert));
endmodule
