// Digital circuit Question_#7.dig as structural Verilog
module Question__7 (
  input  Input,
  input  Clock,
  output Output
);

  wire and_1_out, and_2_out, S_0_q, S_1_nq, S_1_q;

  and and_1 (and_1_out, S_1_nq, S_0_q);
  and and_2 (and_2_out, S_1_q, S_0_q, Input);
  D_FF S_1 (.D(and_1_out), .C(Clock), .Q(S_1_q), .nQ(S_1_nq));
  D_FF S_0 (.D(and_2_out), .C(Clock), .Q(S_0_q));  // open: nQ
  or or_1 (Output, S_1_nq, S_0_q);
endmodule
